// Digital circuit ALU(32bits).dig as structural Verilog
module ALU_32bits (
  input  [31:0] InA,
  input  [31:0] InB,
  input  [3:0] Sel,
  output C1,
  output C2,
  output [31:0] Out
);

  wire SLT_lt, SLTU_lt;
  wire [31:0] ADD_s, and_1_out, bitextender_1_out, bitextender_2_out, or_1_out, SLL_out, SRA_out, SRL_out,
       SUB_s, xor_1_out;

  Add #(.Bits(32)) ADD (.a(InA), .b(InB), .c_i(1'b0), .s(ADD_s), .c_o(C1));
  BarrelShifter #(.Bits(32), .barrelSigned("true")) SLL (.in(InA), .shift(InB[6:0]), .out(SLL_out));
  Comparator #(.Bits(32), .Signed("true")) SLT (.a(InA), .b(InB), .lt(SLT_lt));  // open: gt, eq
  Comparator #(.Bits(32)) SLTU (.a(InA), .b(InB), .lt(SLTU_lt));  // open: gt, eq
  assign xor_1_out = InA ^ InB;  // XOr xor_1, 32 bits wide
  BarrelShifter #(.Bits(32), .barrelSigned("true"), .direction("right")) SRL (
    .in(InA), .shift(InB[6:0]), .out(SRL_out));
  assign and_1_out = InA & InB;  // And and_1, 32 bits wide
  assign or_1_out = InA | InB;  // Or or_1, 32 bits wide
  Sub #(.Bits(32)) SUB (.a(InA), .b(InB), .c_i(1'b0), .s(SUB_s), .c_o(C2));
  BarrelShifter #(.Bits(32), .barrelShifterMode("arithmetic"), .barrelSigned("true"), .direction("right")) SRA (
    .in(InA), .shift(InB[6:0]), .out(SRA_out));
  BitExtender #(.inputBits(1), .outputBits(32)) bitextender_1 (.in(SLT_lt), .out(bitextender_1_out));
  BitExtender #(.inputBits(1), .outputBits(32)) bitextender_2 (.in(SLTU_lt), .out(bitextender_2_out));
  Multiplexer #(.Selector_Bits(4), .Bits(32)) multiplexer_1 (
    .sel(Sel), .in_0(ADD_s), .in_1(SLL_out), .in_2(bitextender_1_out), .in_3(bitextender_2_out),
    .in_4(xor_1_out), .in_5(SRL_out), .in_6(and_1_out), .in_7(or_1_out), .in_8(SUB_s), .in_9({32{1'b0}}),
    .in_10({32{1'b0}}), .in_11({32{1'b0}}), .in_12({32{1'b0}}), .in_13(SRA_out), .in_14({32{1'b0}}),
    .in_15({32{1'b0}}), .out(Out));

  // Notes on the sheet:
  //   InA: Entrada 1 para cualquier operación que se vaya a realizar
  //   InB: Entrada 2 para la operación que se vaya a realizar
  //   C1: Almacena el acarreo de una suma
  //   C2: Acarreo para la resta
  //   Sel: Permite seleccionar la operación que se quiere realizar
  //   Out: Salida dependiendo de la operación escogida
endmodule
