// Digital circuit ALUSplitterDisplay.dig as structural Verilog
module ALUSplitterDisplay (
  input  [31:0] ALUOut,
  output [3:0] D1,
  output [3:0] D2,
  output [3:0] D3,
  output [3:0] D4,
  output [3:0] D5,
  output [3:0] D6,
  output [3:0] D7,
  output [3:0] D8
);


  assign D1 = ALUOut[3:0];
  assign D2 = ALUOut[7:4];
  assign D3 = ALUOut[11:8];
  assign D4 = ALUOut[15:12];
  assign D5 = ALUOut[19:16];
  assign D6 = ALUOut[23:20];
  assign D7 = ALUOut[27:24];
  assign D8 = ALUOut[31:28];

  // Notes on the sheet:
  //   ALUOut: Recibe el resultado de la ALU
  //   D1: Maneja el display 1
  //   D2: Maneja el display 2
  //   D3: Maneja el display 3
  //   D4: Maneja el display 4
  //   D5: Maneja el display 5
  //   D6: Maneja el display 6
  //   D7: Maneja el display 7
  //   D8: Maneja el display 8
endmodule
