// Digital circuit BranchUnit.dig as structural Verilog
module BranchUnit (
  input  [31:0] RU_rs1,
  input  [31:0] RU_rs2,
  input  [4:0] BrOp,
  output NextPCSrc
);

  wire beq, bge, bge_eq, bge_gt, bgeu, bgeu_eq, bgeu_gt, blt, bltu, bne, bne_eq;

  Comparator #(.Signed("true"), .Bits(32)) u_beq (.a(RU_rs1), .b(RU_rs2), .eq(beq));  // open: gt, lt
  Comparator #(.Signed("true"), .Bits(32)) u_bne (.a(RU_rs1), .b(RU_rs2), .eq(bne_eq));  // open: gt, lt
  Comparator #(.Signed("true"), .Bits(32)) u_blt (.a(RU_rs1), .b(RU_rs2), .lt(blt));  // open: gt, eq
  Comparator #(.Signed("true"), .Bits(32)) u_bge (.a(RU_rs1), .b(RU_rs2), .gt(bge_gt), .eq(bge_eq));  // open: lt
  Comparator #(.Bits(32)) u_bltu (.a(RU_rs1), .b(RU_rs2), .lt(bltu));  // open: gt, eq
  Comparator #(.Bits(32)) u_bgeu (.a(RU_rs1), .b(RU_rs2), .gt(bgeu_gt), .eq(bgeu_eq));  // open: lt
  not not_1 (bne, bne_eq);
  or or_1 (bge, bge_gt, bge_eq);
  or or_2 (bgeu, bgeu_gt, bgeu_eq);
  Multiplexer #(.Selector_Bits(5)) multiplexer_1 (
    .sel(BrOp), .in_0(1'b0), .in_1(1'b0), .in_2(1'b0), .in_3(1'b0), .in_4(1'b0), .in_5(1'b0), .in_6(1'b0),
    .in_7(1'b0), .in_8(beq), .in_9(1'b0), .in_10(bne), .in_11(blt), .in_12(1'b0), .in_13(bltu), .in_14(bgeu),
    .in_15(bge), .in_16(1'b1), .in_17(1'b1), .in_18(1'b1), .in_19(1'b1), .in_20(1'b1), .in_21(1'b1),
    .in_22(1'b1), .in_23(1'b1), .in_24(1'b1), .in_25(1'b1), .in_26(1'b1), .in_27(1'b1), .in_28(1'b1),
    .in_29(1'b1), .in_30(1'b1), .in_31(1'b1), .out(NextPCSrc));

  // Other names for the same wires on the sheet: rs1[31:0] = RU_rs1; rs2[31:0] = RU_rs2

  // Notes on the sheet:
  //   RU_rs1: Información del registro rs1
  //   RU_rs2: Información del registro rs2
endmodule
