// Digital circuit DataMemory.dig as structural Verilog
module DataMemory (
  input  [31:0] Addr,
  input  [31:0] DWr,
  input  DMWr,
  input  [2:0] DMCtrl,
  input  clk,
  output [31:0] DRd
);

  RAM32Bits ram32bits_1 (.A(Addr), .D_in(DWr), .we(DMWr), .am(DMCtrl[1:0]), .\signed (DMCtrl[2]), .C(clk), .D_out(DRd));

  // Notes on the sheet:
  //   Addr: Dirección en la cual leer o escribir, dependiendo de si la memoria está habilitada para escribir
  //   DWr: Dato que se piensa escribir o leer de la memoria
  //   DMWr: Habilita la memoria para escribir en ella si está en 1
  //   DMCtrl: Especifica que tipo de lectura hacer. 0 word, 1 half word y 2  byte.
  //   DRd: Valor leído de la memoria en la dirección especificada
endmodule
