// Digital circuit InstructionMemory.dig as structural Verilog
module InstructionMemory (
  input  [23:0] In,
  output [31:0] D_out
);

  EEPROM #(.AddrBits(24), .isProgramMemory("true"), .Bits(32)) eeprom_1 (
    .A(In), .CS(1'b1), .WE(1'b0), .OE(1'b1), .D(D_out));

  // Notes on the sheet:
  //   In: Será la dirección de la cual se quiere extraer una instrucción.
  //   D_out: Instrucción solicitada con la dirección que ofrece el program Counter
endmodule
