// Digital circuit Monocycle_Style.dig as structural Verilog
module Monocycle_Style (
  input  CLK,
  output out_1,
  output out_2,
  output [31:0] out_4,
  output [31:0] out_5,
  output [31:0] IMOut,
  output [31:0] OutPC,
  output [31:0] RU_rs1,
  output [31:0] RU_rs2
);

  wire ALUASrc, ALUBSrc, branchunit_1_nextpcsrc, DMWr, RUWr;
  wire [1:0] RUDataWrSrc;
  wire [2:0] DMCtrl, ImmSrc;
  wire [3:0] ALUOp, D1, D2, D3, D4, D5, D6, D7, D8;
  wire [4:0] BrOp;
  wire [31:0] ALUOut, DataWr, DMOut, InPC, multiplexer_1_out, multiplexer_2_out, RU_rs2_t, SumPC;

  PC_1 pc_1_1 (.clk(CLK), .InPC(InPC), .OutPC(OutPC));
  Add #(.Bits(32)) add_1 (.a(32'h1), .b(OutPC), .c_i(1'b0), .s(SumPC));  // open: c_o
  InstructionMemory instructionmemory_1 (.In(OutPC[23:0]), .D_out(IMOut));
  ALUSplitterDisplay alusplitterdisplay_1 (
    .ALUOut(ALUOut), .D1(D1), .D2(D2), .D3(D3), .D4(D4), .D5(D5), .D6(D6), .D7(D7), .D8(D8));
  Seven_Seg_Hex seven_seg_hex_1 (.d(D8), .dp(1'b0));
  Seven_Seg_Hex seven_seg_hex_2 (.d(D7), .dp(1'b0));
  ControlUnit controlunit_1 (
    .Opcode(IMOut[6:0]), .Funct3(IMOut[14:12]), .Funct7(IMOut[31:25]), .RUWr(RUWr), .ImmSrc(ImmSrc),
    .ALUASrc(ALUASrc), .ALUBSrc(ALUBSrc), .DMWr(DMWr), .RUDataWrSrc(RUDataWrSrc), .BrOp(BrOp),
    .DMCtrl(DMCtrl), .ALUOp(ALUOp));
  RegisterUnit registerunit_1 (
    .RD(IMOut[11:7]), .C(CLK), .RS1(IMOut[19:15]), .DataWr(DataWr), .RS2(IMOut[24:20]), .RuWr(RUWr),
    .RU_rs1(RU_rs1), .RU_rs2(RU_rs2_t));
  ImmGen immgen_1 (.Inst_31_7(IMOut[31:7]), .ImmSrc(ImmSrc), .ImmExt(out_4));
  Seven_Seg_Hex seven_seg_hex_3 (.d(D6), .dp(1'b0));
  Seven_Seg_Hex seven_seg_hex_4 (.d(D5), .dp(1'b0));
  Seven_Seg_Hex seven_seg_hex_5 (.d(D4), .dp(1'b0));
  Multiplexer #(.Bits(32)) multiplexer_1 (.sel(ALUASrc), .in_0(RU_rs1), .in_1(OutPC), .out(multiplexer_1_out));
  Multiplexer #(.Bits(32)) multiplexer_2 (.sel(ALUBSrc), .in_0(RU_rs2_t), .in_1(out_4), .out(multiplexer_2_out));
  Seven_Seg_Hex seven_seg_hex_6 (.d(D3), .dp(1'b0));
  BranchUnit branchunit_1 (.RU_rs1(RU_rs1), .RU_rs2(RU_rs2_t), .BrOp(BrOp), .NextPCSrc(branchunit_1_nextpcsrc));
  Seven_Seg_Hex seven_seg_hex_7 (.d(D2), .dp(1'b0));
  Seven_Seg_Hex seven_seg_hex_8 (.d(D1), .dp(1'b0));
  ALU_32bits alu_32bits_1 (
    .InA(multiplexer_1_out), .InB(multiplexer_2_out), .Sel(ALUOp), .C1(out_1), .C2(out_2), .Out(ALUOut));
  Multiplexer #(.Bits(32)) multiplexer_3 (.sel(branchunit_1_nextpcsrc), .in_0(SumPC), .in_1(ALUOut), .out(InPC));
  DataMemory datamemory_1 (.Addr(ALUOut), .DWr(RU_rs2_t), .DMWr(DMWr), .DMCtrl(DMCtrl), .clk(CLK), .DRd(DMOut));
  Multiplexer #(.Selector_Bits(2), .Bits(32)) multiplexer_4 (
    .sel(RUDataWrSrc), .in_0(ALUOut), .in_1(DMOut), .in_2(SumPC), .in_3({32{1'b0}}), .out(DataWr));

  assign out_5 = IMOut;
  assign RU_rs2 = RU_rs1;

  // Other names for the same wires on the sheet: C1 = out_1; C2 = out_2; ImmExt[31:0] = out_4;
  //   Opcode[6:0] = IMOut[6:0]; RD[4:0] = IMOut[11:7]; Funct3[2:0] = IMOut[14:12]; RS1[4:0] = IMOut[19:15];
  //   RS2[4:0] = IMOut[24:20]; Funct7[6:0] = IMOut[31:25]
endmodule
