// Digital circuit PC(1).dig as structural Verilog
module PC_1 (
  input  clk,
  input  [31:0] InPC,
  output [31:0] OutPC
);

  Register #(.Bits(32)) register_1 (.D(InPC), .C(clk), .en(1'b1), .Q(OutPC));
endmodule
